# Fritzing sketch W10-TSL2561 (saved by Fritzing 0.9.0b)

parts:
  TSL2561 = _TL2561
  Raspberry_Pi1 = Raspberry Pi B rev2

nets:
  GND: TSL2561.GND, Raspberry_Pi1.GND
  N1: TSL2561.SCL, Raspberry_Pi1.GPIO_3
  N2: TSL2561.SDA, Raspberry_Pi1.GPIO_2
  VCC: TSL2561.Vcc, Raspberry_Pi1.3V3

custom parts:
  : Sensor de Luminosidade - TL2561
